# Fritzing sketch esp relays (saved by Fritzing 0.9.3b)
breadboards: 1

parts:
  ESP8266 = NodeMCU V1.0
  LED1 = smd LED [color="Green (555nm)" package="0805 [SMD]"]
  LED2 = smd LED [color="Red (633nm)" package="0805 [SMD]"]
  LED1_2 = smd LED [color="Green (555nm)" package="0805 [SMD]"]
  LED6 = smd LED [color="Red (633nm)" package="0805 [SMD]"]
  4-Channel_Relay = 4-Channel 5v Relay Shield [package=relay-4ch5v10a]

nets (from the breadboard view):
  N1: ESP8266.D4, LED6.anode
  N2: ESP8266.3V3, LED1.anode, LED2.anode, LED1_2.anode
  N3: ESP8266.GND, LED6.cathode
  N4: ESP8266.D5, LED1.cathode, 4-Channel_Relay.IN1
  N5: ESP8266.D6, LED1_2.cathode, 4-Channel_Relay.IN2
  N6: ESP8266.D7, LED2.cathode, 4-Channel_Relay.IN3
  N7: ESP8266.D8, 4-Channel_Relay.IN4

notes:
  To TTL 3V3
  Output 1
  Output 2
  Power source
  Inverter switch
  Magnet Sensor SCL
  Magnet Sensor SDA
  Note: Schematic view of 4-channel relay is not optimized
  D1 -> SDA (On magnet sensor)
  D2 -> SCL

custom parts:
  NodeMCU V1.0: ESP8266 based NodeMCU
  4-Channel 5v Relay Shield: 4 Channel 5v Relay Shield w. 2x SPD-06VDC-SD-C
